# Fritzing sketch Wiring (saved by Fritzing 1.0.5)
circuit board: 42.7251cm x 15.7796cm
stripboards: 1

parts:
  Mod1 = Raspberry Pi Pico
  Mod2 = Raspberry Pi 4B  # not connected
  Motortreiber_01 = Motor Driver 1A Dual TB6612FNG
  Bauteil2 = Motor Driver 1A Dual TB6612FNG
  DC_Mot_Enc1 = DC Motor with two-phase hall-encoder [part_number=VT-E-G25A-06-177E]
  BAT1 = LiPo 3S 11,1V 2200mAh 25C
  DC_Mot_Enc3 = DC Motor with two-phase hall-encoder [part_number=VT-E-G25A-06-177E]
  DC_Mot_Enc4 = DC Motor with two-phase hall-encoder [part_number=VT-E-G25A-06-177E]
  DC_Mot_Enc2 = DC Motor with two-phase hall-encoder [part_number=VT-E-G25A-06-177E]
  M1 = RPlidar A1M8 [package=THT]  # not connected
  M2 = ESC
  920KV_Motor1 = DJI 920 KV Motor
  920KV_Motor2 = DJI 920 KV Motor
  J1 = Basic Servo
  M4 = RioRand LM2596
  M5 = RioRand LM2596
  M6 = RioRand LM2596
  S1 = Taiway 100-SP-X-T1 SPDT Miniature Toggle Switch [part_number=100-SP-X-T1-0-0-B1-M1 package=THT]
  M3 = ESC

nets (from the breadboard view):
  N1: Mod1.pin_1, Motortreiber_01.STBY, Bauteil2.STBY
  N2: Mod1.pin_4, Motortreiber_01.PWMA
  N3: Mod1.pin_5, Motortreiber_01.PWMB
  N4: Mod1.pin_6, Bauteil2.PWMA
  N5: Mod1.pin_7, Bauteil2.PWMB
  N6: Mod1.pin_9, DC_Mot_Enc4.pin3
  N7: Mod1.pin_10, DC_Mot_Enc4.pin4
  N8: Mod1.pin_11, DC_Mot_Enc1.pin3
  N9: Mod1.pin_12, DC_Mot_Enc1.pin4
  N10: Mod1.pin_14, DC_Mot_Enc2.pin4
  N11: Mod1.pin_15, DC_Mot_Enc2.pin3
  N12: Mod1.pin_16, DC_Mot_Enc3.pin3
  N13: Mod1.pin_17, DC_Mot_Enc3.pin4
  N14: Mod1.pin_19, M2.DATA
  N15: Mod1.pin_20, M3.DATA
  N16: Mod1.pin_21, J1.pulse
  N17: Mod1.pin_22, Motortreiber_01.BIN2
  N18: Mod1.pin_24, Motortreiber_01.AIN2
  N19: Mod1.pin_25, Motortreiber_01.AIN1
  N20: Mod1.pin_26, Motortreiber_01.BIN1
  N21: Mod1.pin_27, Bauteil2.AIN1
  N22: Mod1.pin_29, Bauteil2.AIN2
  N23: Mod1.pin_31, Bauteil2.BIN2
  N24: Mod1.pin_32, Bauteil2.BIN1
  N25: Mod1.pin_36, DC_Mot_Enc1.pin2, DC_Mot_Enc3.pin2, DC_Mot_Enc4.pin2, DC_Mot_Enc2.pin2
  GND: Motortreiber_01.GND, Bauteil2.GND, DC_Mot_Enc1.pin5, DC_Mot_Enc3.pin5, DC_Mot_Enc4.pin5, DC_Mot_Enc2.pin5, M5.Pin_4, M6.Pin_4
  N26: Motortreiber_01.B01, DC_Mot_Enc3.pin1
  N27: Motortreiber_01.B02, DC_Mot_Enc3.pin6
  N28: Motortreiber_01.A02, DC_Mot_Enc1.pin6
  N29: Motortreiber_01.A01, DC_Mot_Enc1.pin1
  N30: Motortreiber_01.VCC, M6.Pin_3
  N31: Bauteil2.B01, DC_Mot_Enc4.pin6
  N32: Bauteil2.B02, DC_Mot_Enc4.pin1
  N33: Bauteil2.A02, DC_Mot_Enc2.pin1
  N34: Bauteil2.A01, DC_Mot_Enc2.pin6
  N35: Bauteil2.VCC, M5.Pin_3
  N36: BAT1.positive, S1.L1
  GND_2: BAT1.negative, M2.GND, M4.Pin_2, M6.Pin_2, M3.GND
  N37: M2.U, 920KV_Motor1.u
  N38: M2.V, 920KV_Motor1.v
  N39: M2.W, 920KV_Motor1.w
  N40: 920KV_Motor2.w, M3.W
  N41: 920KV_Motor2.v, M3.V
  N42: 920KV_Motor2.u, M3.U
  N43: J1.gnd, M4.Pin_4
  N44: J1.vcc, M4.Pin_3
  N45: M4.Pin_1, M6.Pin_1, S1.L2

notes:
  BLDC
  ESC
  5V

custom parts:
  Raspberry Pi Pico: Raspberry Pi Pico. Based around the RP2040 microcontroller the Pico is a low cost microcontroller device bringing Raspberry Pi quality, cost, and easy of use to the microcontroller space. Jan 2021, Split part in to two versions: tht (this one) and SMD. This one will drill holes for a .1 in header in pcb to allow plugging in the module as well as providing pads to solder the module to the top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
  RPlidar A1M8: .The RPLIDAR A1 is the next generation low cost 360 degree 2D laser scanner (LIDAR) solution developed by SLAMTEC. It can take up to 4000 samples of laser ranging per second with high rotation speed. And equipped with SLAMTEC patented OPTMAG technology, it breakouts the life limitation of traditional LIDAR system so as to work stably for a long time.
  DJI 920 KV Motor: DJI Brushless Outrunner 2212/920K Motor F330-550
